// Logisim project COMP303_TermProject_Ayberk_SORGUN_Ceren_KOCAOGULLAR.circ as structural Verilog: 13 circuits, main circuit main
// ALUcum
module main (
  input  [15:0] Input_A,
  input  [15:0] Input_B,
  input  [5:0] Opcode,
  output Zero,
  output [15:0] Output,
  output Overflow,
  output Carryout
);

  wire carry_add, carry_sub, comparator_2_eq, comparator_2_lt, multiplexer_4_out, multiplexer_5_out,
       overflow_add, overflow_addi, overflow_sll, overflow_sub;
  wire [0:0] blez_res, comparator_1_eq, comparator_3_gt;
  wire [15:0] abstract_value_2_output, and_out, Hi_output, Lo_output, multiplexer_1_out, multiplexer_2_out,
       multiplier_1_cout, multiplier_1_out, n16bitadder_1__16_bit_output, or_2_out, shifter_1_out, Subresult;

  abstract_value abstract_value_1 ();  // open: Input, Output, Flipped
  Shifter #(.width(16)) shifter_1 (.in(Input_A), .\dist (Input_B[9:6]), .out(shifter_1_out));
  Comparator #(.width(16)) comparator_1 (.a(Input_A), .b(Input_B), .eq(comparator_1_eq[0]));  // open: gt, lt
  Comparator #(.width(16)) comparator_2 (
    .a(Input_A), .b({16{1'b0}}), .eq(comparator_2_eq), .lt(comparator_2_lt));  // open: gt
  Comparator #(.width(16)) comparator_3 (.a(Input_A), .b(Input_B), .gt(comparator_3_gt[0]));  // open: eq, lt
  abstract_value abstract_value_2 (.Input(Input_A), .Output(abstract_value_2_output));  // open: Flipped
  or or_1 (blez_res[0], comparator_2_eq, comparator_2_lt);
  Multiplier #(.width(16)) multiplier_1 (
    .a(Input_A), .b(Input_B), .out(multiplier_1_out), .cout(multiplier_1_cout));  // open: cin
  _16BitAdder u_16bitadder_1 (
    ._16_bit_A(Input_A), ._16_bit_B(Input_B), ._16_bit_output(n16bitadder_1__16_bit_output),
    .Carryout(carry_add), .Overflow(overflow_add));
  _16BitSubtractor u_16bitsubtractor (
    ._16_bit_A(Input_A), ._16_bit_B(Input_B), ._16_bit_output(Subresult), .Carryout(carry_sub),
    .Overflow(overflow_sub));
  assign and_out = Input_A & Input_B;  // AND_Gate and, 16 bits wide
  assign or_2_out = Input_A | Input_B;  // OR_Gate or_2, 16 bits wide
  IORegister Hi (.Input(multiplier_1_cout), .Output(Hi_output));
  IORegister Lo (.Input(multiplier_1_out), .Output(Lo_output));
  Multiplexer #(.select(4), .width(16), .enable("false")) multiplexer_1 (
    .in0(shifter_1_out), .in1({16{1'b0}}), .in2({{15{1'b0}}, comparator_1_eq[0]}),
    .in3({{15{1'b0}}, blez_res[0]}), .in4(n16bitadder_1__16_bit_output), .in5({16{1'b0}}), .in6({16{1'b0}}),
    .in7({16{1'b0}}), .in8(Hi_output), .in9(Lo_output), .in10({16{1'b0}}), .in11({16{1'b0}}),
    .in12(multiplier_1_out), .in13({16{1'b0}}), .in14({16{1'b0}}), .in15({16{1'b0}}),
    .out(multiplexer_1_out), .sel(Opcode[4:1]));
  Multiplexer #(.select(4), .width(16), .enable("false")) multiplexer_2 (
    .in0(n16bitadder_1__16_bit_output), .in1({16{1'b0}}), .in2(Subresult),
    .in3(n16bitadder_1__16_bit_output), .in4(and_out), .in5(or_2_out), .in6({16{1'b0}}), .in7({16{1'b0}}),
    .in8({16{1'b0}}), .in9({16{1'b0}}), .in10({{15{1'b0}}, comparator_3_gt[0]}), .in11(Input_A),
    .in12({16{1'b0}}), .in13({16{1'b0}}), .in14({16{1'b0}}), .in15(abstract_value_2_output),
    .out(multiplexer_2_out), .sel(Opcode[3:0]));
  Multiplexer #(.width(16), .enable("false")) multiplexer_3 (
    .in0(multiplexer_1_out), .in1(multiplexer_2_out), .out(Output), .sel(Opcode[5]));
  Multiplexer #(.select(4), .enable("false")) multiplexer_4 (
    .in0(overflow_sll), .in1(1'b0), .in2(1'b0), .in3(1'b0), .in4(overflow_addi), .in5(1'b0), .in6(1'b0),
    .in7(1'b0), .in8(1'b0), .in9(1'b0), .in10(1'b0), .in11(1'b0), .in12(1'b0), .in13(1'b0), .in14(1'b0),
    .in15(1'b0), .out(multiplexer_4_out), .sel(Opcode[4:1]));
  Multiplexer #(.select(4), .enable("false")) multiplexer_5 (
    .in0(overflow_add), .in1(1'b0), .in2(overflow_sub), .in3(1'b0), .in4(1'b0), .in5(1'b0), .in6(1'b0),
    .in7(1'b0), .in8(1'b0), .in9(1'b0), .in10(1'b0), .in11(1'b0), .in12(1'b0), .in13(1'b0), .in14(1'b0),
    .in15(1'b0), .out(multiplexer_5_out), .sel(Opcode[3:0]));
  Multiplexer #(.select(4)) multiplexer_6 (
    .in0(carry_add), .in1(1'b0), .in2(carry_sub), .in3(1'b0), .in4(1'b0), .in5(1'b0), .in6(1'b0), .in7(1'b0),
    .in8(1'b0), .in9(1'b0), .in10(1'b0), .in11(1'b0), .in12(1'b0), .in13(1'b0), .in14(1'b0), .in15(1'b0),
    .out(Carryout), .sel(Opcode[4:1]), .en(Opcode[5]));
  or or_3 (Zero, Output[0], Output[1], Output[2], Output[3], Output[4], Output[5], Output[6], Output[7], Output[9], Output[10], Output[11], Output[12], Output[13], Output[14], Output[15], Output[8]);
  Multiplexer #(.enable("false")) multiplexer_7 (
    .in0(multiplexer_4_out), .in1(multiplexer_5_out), .out(Overflow), .sel(Opcode[5]));

  // Other names for the same wires on the sheet: A[15:0] = Input_A; B[15:0] = Input_B
endmodule

// +
module _16BitAdder (
  input  [15:0] _16_bit_A,
  input  [15:0] _16_bit_B,
  output [15:0] _16_bit_output,
  output Carryout,
  output Overflow
);

  wire n1bitadder_1_carry_out, n1bitadder_2_carry_out, n1bitadder_3_carry_out, n1bitadder_4_carry_out,
       n1bitadder_5_carry_out, n1bitadder_6_carry_out, n1bitadder_7_carry_out, n1bitadder_8_carry_out,
       n1bitadder_9_carry_out, n1bitadder_10_carry_out, n1bitadder_11_carry_out, n1bitadder_12_carry_out,
       n1bitadder_13_carry_out, n1bitadder_14_carry_out, n1bitadder_15_carry_out, xor_1_out, xor_2_out;

  _1BitAdder u_1bitadder_1 (
    .A(_16_bit_A[0]), .B(_16_bit_B[0]), .Carry(1'b0), .Sum(_16_bit_output[0]),
    .Carry_Out(n1bitadder_1_carry_out));
  _1BitAdder u_1bitadder_2 (
    .A(_16_bit_A[1]), .B(_16_bit_B[1]), .Carry(n1bitadder_1_carry_out), .Sum(_16_bit_output[1]),
    .Carry_Out(n1bitadder_2_carry_out));
  _1BitAdder u_1bitadder_3 (
    .A(_16_bit_A[2]), .B(_16_bit_B[2]), .Carry(n1bitadder_2_carry_out), .Sum(_16_bit_output[2]),
    .Carry_Out(n1bitadder_3_carry_out));
  _1BitAdder u_1bitadder_4 (
    .A(_16_bit_A[3]), .B(_16_bit_B[3]), .Carry(n1bitadder_3_carry_out), .Sum(_16_bit_output[3]),
    .Carry_Out(n1bitadder_4_carry_out));
  _1BitAdder u_1bitadder_5 (
    .A(_16_bit_A[4]), .B(_16_bit_B[4]), .Carry(n1bitadder_4_carry_out), .Sum(_16_bit_output[4]),
    .Carry_Out(n1bitadder_5_carry_out));
  _1BitAdder u_1bitadder_6 (
    .A(_16_bit_A[5]), .B(_16_bit_B[5]), .Carry(n1bitadder_5_carry_out), .Sum(_16_bit_output[5]),
    .Carry_Out(n1bitadder_6_carry_out));
  _1BitAdder u_1bitadder_7 (
    .A(_16_bit_A[6]), .B(_16_bit_B[6]), .Carry(n1bitadder_6_carry_out), .Sum(_16_bit_output[6]),
    .Carry_Out(n1bitadder_7_carry_out));
  _1BitAdder u_1bitadder_8 (
    .A(_16_bit_A[7]), .B(_16_bit_B[7]), .Carry(n1bitadder_7_carry_out), .Sum(_16_bit_output[7]),
    .Carry_Out(n1bitadder_8_carry_out));
  _1BitAdder u_1bitadder_9 (
    .A(_16_bit_A[8]), .B(_16_bit_B[8]), .Carry(n1bitadder_8_carry_out), .Sum(_16_bit_output[8]),
    .Carry_Out(n1bitadder_9_carry_out));
  _1BitAdder u_1bitadder_10 (
    .A(_16_bit_A[9]), .B(_16_bit_B[9]), .Carry(n1bitadder_9_carry_out), .Sum(_16_bit_output[9]),
    .Carry_Out(n1bitadder_10_carry_out));
  _1BitAdder u_1bitadder_11 (
    .A(_16_bit_A[10]), .B(_16_bit_B[10]), .Carry(n1bitadder_10_carry_out), .Sum(_16_bit_output[10]),
    .Carry_Out(n1bitadder_11_carry_out));
  _1BitAdder u_1bitadder_12 (
    .A(_16_bit_A[11]), .B(_16_bit_B[11]), .Carry(n1bitadder_11_carry_out), .Sum(_16_bit_output[11]),
    .Carry_Out(n1bitadder_12_carry_out));
  _1BitAdder u_1bitadder_13 (
    .A(_16_bit_A[12]), .B(_16_bit_B[12]), .Carry(n1bitadder_12_carry_out), .Sum(_16_bit_output[12]),
    .Carry_Out(n1bitadder_13_carry_out));
  _1BitAdder u_1bitadder_14 (
    .A(_16_bit_A[13]), .B(_16_bit_B[13]), .Carry(n1bitadder_13_carry_out), .Sum(_16_bit_output[13]),
    .Carry_Out(n1bitadder_14_carry_out));
  _1BitAdder u_1bitadder_15 (
    .A(_16_bit_A[14]), .B(_16_bit_B[14]), .Carry(n1bitadder_14_carry_out), .Sum(_16_bit_output[14]),
    .Carry_Out(n1bitadder_15_carry_out));
  _1BitAdder u_1bitadder_16 (
    .A(_16_bit_A[15]), .B(_16_bit_B[15]), .Carry(n1bitadder_15_carry_out), .Sum(_16_bit_output[15]),
    .Carry_Out(Carryout));
  xor xor_1 (xor_1_out, _16_bit_A[15], _16_bit_B[15]);
  xor xor_2 (xor_2_out, _16_bit_output[15], _16_bit_A[15]);
  Multiplexer #(.enable("false")) multiplexer_1 (.in0(xor_2_out), .in1(1'b0), .out(Overflow), .sel(xor_1_out));
endmodule

// slt
module _16bitSetLessThan (
  input  [15:0] _16BitA,
  input  [15:0] _16BitB,
  output [15:0] _16BitC
);

  wire [14:0] subtractor_1_out;

  Subtractor #(.width(16)) subtractor_1 (
    .a(_16BitA), .b(_16BitB), .out({_16BitC[0], subtractor_1_out}));  // open: bin, bout

  assign _16BitC[15:1] = {15{1'b0}};
endmodule

// beq
module _16BitBranchEqual (
  input  [15:0] _16BitA,
  input  [15:0] _16BitB,
  output [15:0] Out
);

  wire [15:0] subtractor_1_out;

  Subtractor #(.width(16)) subtractor_1 (.a(_16BitA), .b(_16BitB), .out(subtractor_1_out));  // open: bin, bout
  nor nor_1 (Out[0], subtractor_1_out[7], subtractor_1_out[0], subtractor_1_out[1], subtractor_1_out[2], subtractor_1_out[3], subtractor_1_out[4], subtractor_1_out[5], subtractor_1_out[6], subtractor_1_out[8], subtractor_1_out[9], subtractor_1_out[10], subtractor_1_out[11], subtractor_1_out[12], subtractor_1_out[13], subtractor_1_out[14], subtractor_1_out[15]);

  assign Out[15:1] = {15{1'b0}};
endmodule

module GatedLatch (
  input  DataInput,
  input  WriteEnable,
  output DataOutput
);

  wire and_1_out, and_2_out, not_1_out, not_2_out, or_1_out;

  not not_1 (not_1_out, DataInput);
  and and_1 (and_1_out, DataInput, WriteEnable);
  and and_2 (and_2_out, not_1_out, WriteEnable);
  or or_1 (or_1_out, DataOutput, and_1_out);
  not not_2 (not_2_out, and_2_out);
  and and_3 (DataOutput, or_1_out, not_2_out);
endmodule

// 16br
module _16BitRegister (
  input  WriteEnable,
  input  [15:0] Input,
  output [15:0] Output
);

  GatedLatch gatedlatch_1 (.DataInput(Input[15]), .WriteEnable(WriteEnable), .DataOutput(Output[15]));
  GatedLatch gatedlatch_2 (.DataInput(Input[14]), .WriteEnable(WriteEnable), .DataOutput(Output[14]));
  GatedLatch gatedlatch_3 (.DataInput(Input[13]), .WriteEnable(WriteEnable), .DataOutput(Output[13]));
  GatedLatch gatedlatch_4 (.DataInput(Input[11]), .WriteEnable(WriteEnable), .DataOutput(Output[11]));
  GatedLatch gatedlatch_5 (.DataInput(Input[12]), .WriteEnable(WriteEnable), .DataOutput(Output[12]));
  GatedLatch gatedlatch_6 (.DataInput(Input[10]), .WriteEnable(WriteEnable), .DataOutput(Output[10]));
  GatedLatch gatedlatch_7 (.DataInput(Input[9]), .WriteEnable(WriteEnable), .DataOutput(Output[9]));
  GatedLatch gatedlatch_8 (.DataInput(Input[7]), .WriteEnable(WriteEnable), .DataOutput(Output[7]));
  GatedLatch gatedlatch_9 (.DataInput(Input[8]), .WriteEnable(WriteEnable), .DataOutput(Output[8]));
  GatedLatch gatedlatch_10 (.DataInput(Input[5]), .WriteEnable(WriteEnable), .DataOutput(Output[5]));
  GatedLatch gatedlatch_11 (.DataInput(Input[6]), .WriteEnable(WriteEnable), .DataOutput(Output[6]));
  GatedLatch gatedlatch_12 (.DataInput(Input[3]), .WriteEnable(WriteEnable), .DataOutput(Output[3]));
  GatedLatch gatedlatch_13 (.DataInput(Input[4]), .WriteEnable(WriteEnable), .DataOutput(Output[4]));
  GatedLatch gatedlatch_14 (.DataInput(Input[1]), .WriteEnable(WriteEnable), .DataOutput(Output[1]));
  GatedLatch gatedlatch_15 (.DataInput(Input[2]), .WriteEnable(WriteEnable), .DataOutput(Output[2]));
  GatedLatch gatedlatch_16 (.DataInput(Input[0]), .WriteEnable(WriteEnable), .DataOutput(Output[0]));
endmodule

module Register (
  input  [2:0] ReadAddress1,
  input  [2:0] ReadAddress2,
  input  WriteEnable,
  input  [2:0] WriteAddress,
  input  [15:0] RegisterData,
  input  Clockin,
  output [15:0] ReadData1,
  output [15:0] ReadData2
);

  wire and_1_out, and_2_out, and_3_out, and_4_out, and_5_out, and_6_out, and_7_out, and_8_out,
       decoder_1_out0, decoder_1_out1, decoder_1_out2, decoder_1_out3, decoder_1_out4, decoder_1_out5,
       decoder_1_out6, decoder_1_out7;
  wire [15:0] register_1_q, register_2_q, register_3_q, register_4_q, register_5_q, register_6_q,
       register_7_q, register_8_q;

  Decoder #(.select(3), .enable("false")) decoder_1 (
    .out0(decoder_1_out0), .out1(decoder_1_out1), .out2(decoder_1_out2), .out3(decoder_1_out3),
    .out4(decoder_1_out4), .out5(decoder_1_out5), .out6(decoder_1_out6), .out7(decoder_1_out7),
    .sel(WriteAddress));
  and and_1 (and_1_out, WriteEnable, decoder_1_out0);
  and and_2 (and_2_out, WriteEnable, decoder_1_out1);
  and and_3 (and_3_out, WriteEnable, decoder_1_out2);
  and and_4 (and_4_out, WriteEnable, decoder_1_out3);
  and and_5 (and_5_out, WriteEnable, decoder_1_out4);
  and and_6 (and_6_out, WriteEnable, decoder_1_out5);
  and and_7 (and_7_out, WriteEnable, decoder_1_out6);
  and and_8 (and_8_out, WriteEnable, decoder_1_out7);
  Register_part #(.width(16)) register_1 (
    .D(RegisterData), .en(and_1_out), .Q(register_1_q), .clk(Clockin));  // open: clr
  Register_part #(.width(16)) register_2 (
    .D(RegisterData), .en(and_2_out), .Q(register_2_q), .clk(Clockin));  // open: clr
  Register_part #(.width(16)) register_3 (
    .D(RegisterData), .en(and_3_out), .Q(register_3_q), .clk(Clockin));  // open: clr
  Register_part #(.width(16)) register_4 (
    .D(RegisterData), .en(and_4_out), .Q(register_4_q), .clk(Clockin));  // open: clr
  Register_part #(.width(16)) register_5 (
    .D(RegisterData), .en(and_5_out), .Q(register_5_q), .clk(Clockin));  // open: clr
  Register_part #(.width(16)) register_6 (
    .D(RegisterData), .en(and_6_out), .Q(register_6_q), .clk(Clockin));  // open: clr
  Register_part #(.width(16)) register_7 (
    .D(RegisterData), .en(and_7_out), .Q(register_7_q), .clk(Clockin));  // open: clr
  Register_part #(.width(16)) register_8 (
    .D(RegisterData), .en(and_8_out), .Q(register_8_q), .clk(Clockin));  // open: clr
  Multiplexer #(.select(3), .width(16), .enable("false")) multiplexer_1 (
    .in0(register_1_q), .in1(register_2_q), .in2(register_3_q), .in3(register_4_q), .in4(register_5_q),
    .in5(register_6_q), .in6(register_7_q), .in7(register_8_q), .out(ReadData1), .sel(ReadAddress1));
  Multiplexer #(.select(3), .width(16), .enable("false")) multiplexer_2 (
    .in0(register_1_q), .in1(register_2_q), .in2(register_3_q), .in3(register_4_q), .in4(register_5_q),
    .in5(register_6_q), .in6(register_7_q), .in7(register_8_q), .out(ReadData2), .sel(ReadAddress2));
endmodule

module ImmediateSelect (
  input  [15:0] Immediate,
  input  [15:0] Input,
  input  [2:0] Select,
  output [15:0] Input_B
);

  Multiplexer #(.select(3), .width(16), .enable("false")) multiplexer_1 (
    .in0(Input), .in1(Immediate), .in2(Input), .in3(Input), .in4(Input), .in5(Input), .in6(Input),
    .in7(Input), .out(Input_B), .sel(Select));
endmodule

module IORegister (
  input  [15:0] Input,
  output [15:0] Output
);


  assign Output = Input;
endmodule

module _1BitAdder (
  input  A,
  input  B,
  input  Carry,
  output Sum,
  output Carry_Out
);

  wire and_1_out, and_2_out, xor_1_out;

  xor xor_1 (xor_1_out, A, B);
  xor xor_2 (Sum, xor_1_out, Carry);
  and and_1 (and_1_out, Carry, xor_1_out);
  and and_2 (and_2_out, A, B);
  or or_1 (Carry_Out, and_1_out, and_2_out);

  // Other names for the same wires on the sheet: C = Carry
endmodule

// -
module _16BitSubtractor (
  input  [15:0] _16_bit_A,
  input  [15:0] _16_bit_B,
  output [15:0] _16_bit_output,
  output Carryout,
  output Overflow
);

  wire n1bitadder_1_carry_out, n1bitadder_2_carry_out, n1bitadder_3_carry_out, n1bitadder_4_carry_out,
       n1bitadder_5_carry_out, n1bitadder_6_carry_out, n1bitadder_7_carry_out, n1bitadder_8_carry_out,
       n1bitadder_9_carry_out, n1bitadder_10_carry_out, n1bitadder_11_carry_out, n1bitadder_12_carry_out,
       n1bitadder_13_carry_out, n1bitadder_14_carry_out, n1bitadder_15_carry_out, xor_1_out, xor_2_out;
  wire [15:0] not_1_out;

  assign not_1_out = ~_16_bit_B;  // NOT_Gate not_1, 16 bits wide
  _1BitAdder u_1bitadder_1 (
    .A(_16_bit_A[0]), .B(not_1_out[0]), .Carry(1'b1), .Sum(_16_bit_output[0]),
    .Carry_Out(n1bitadder_1_carry_out));
  _1BitAdder u_1bitadder_2 (
    .A(_16_bit_A[1]), .B(not_1_out[1]), .Carry(n1bitadder_1_carry_out), .Sum(_16_bit_output[1]),
    .Carry_Out(n1bitadder_2_carry_out));
  _1BitAdder u_1bitadder_3 (
    .A(_16_bit_A[2]), .B(not_1_out[2]), .Carry(n1bitadder_2_carry_out), .Sum(_16_bit_output[2]),
    .Carry_Out(n1bitadder_3_carry_out));
  _1BitAdder u_1bitadder_4 (
    .A(_16_bit_A[3]), .B(not_1_out[3]), .Carry(n1bitadder_3_carry_out), .Sum(_16_bit_output[3]),
    .Carry_Out(n1bitadder_4_carry_out));
  _1BitAdder u_1bitadder_5 (
    .A(_16_bit_A[4]), .B(not_1_out[4]), .Carry(n1bitadder_4_carry_out), .Sum(_16_bit_output[4]),
    .Carry_Out(n1bitadder_5_carry_out));
  _1BitAdder u_1bitadder_6 (
    .A(_16_bit_A[5]), .B(not_1_out[5]), .Carry(n1bitadder_5_carry_out), .Sum(_16_bit_output[5]),
    .Carry_Out(n1bitadder_6_carry_out));
  _1BitAdder u_1bitadder_7 (
    .A(_16_bit_A[6]), .B(not_1_out[6]), .Carry(n1bitadder_6_carry_out), .Sum(_16_bit_output[6]),
    .Carry_Out(n1bitadder_7_carry_out));
  _1BitAdder u_1bitadder_8 (
    .A(_16_bit_A[7]), .B(not_1_out[7]), .Carry(n1bitadder_7_carry_out), .Sum(_16_bit_output[7]),
    .Carry_Out(n1bitadder_8_carry_out));
  _1BitAdder u_1bitadder_9 (
    .A(_16_bit_A[8]), .B(not_1_out[8]), .Carry(n1bitadder_8_carry_out), .Sum(_16_bit_output[8]),
    .Carry_Out(n1bitadder_9_carry_out));
  _1BitAdder u_1bitadder_10 (
    .A(_16_bit_A[9]), .B(not_1_out[9]), .Carry(n1bitadder_9_carry_out), .Sum(_16_bit_output[9]),
    .Carry_Out(n1bitadder_10_carry_out));
  _1BitAdder u_1bitadder_11 (
    .A(_16_bit_A[10]), .B(not_1_out[10]), .Carry(n1bitadder_10_carry_out), .Sum(_16_bit_output[10]),
    .Carry_Out(n1bitadder_11_carry_out));
  _1BitAdder u_1bitadder_12 (
    .A(_16_bit_A[11]), .B(not_1_out[11]), .Carry(n1bitadder_11_carry_out), .Sum(_16_bit_output[11]),
    .Carry_Out(n1bitadder_12_carry_out));
  _1BitAdder u_1bitadder_13 (
    .A(_16_bit_A[12]), .B(not_1_out[12]), .Carry(n1bitadder_12_carry_out), .Sum(_16_bit_output[12]),
    .Carry_Out(n1bitadder_13_carry_out));
  _1BitAdder u_1bitadder_14 (
    .A(_16_bit_A[13]), .B(not_1_out[13]), .Carry(n1bitadder_13_carry_out), .Sum(_16_bit_output[13]),
    .Carry_Out(n1bitadder_14_carry_out));
  _1BitAdder u_1bitadder_15 (
    .A(_16_bit_A[14]), .B(not_1_out[14]), .Carry(n1bitadder_14_carry_out), .Sum(_16_bit_output[14]),
    .Carry_Out(n1bitadder_15_carry_out));
  _1BitAdder u_1bitadder_16 (
    .A(_16_bit_A[15]), .B(not_1_out[15]), .Carry(n1bitadder_15_carry_out), .Sum(_16_bit_output[15]),
    .Carry_Out(Carryout));
  xor xor_1 (xor_1_out, _16_bit_A[15], not_1_out[15]);
  xor xor_2 (xor_2_out, _16_bit_output[15], _16_bit_A[15]);
  Multiplexer #(.enable("false")) multiplexer_1 (.in0(xor_2_out), .in1(1'b0), .out(Overflow), .sel(xor_1_out));
endmodule

module CPU (
  input  in_1,
  output [31:0] Instruction
);

  wire AluSrc, Branch, Clock, Memrd, Memtoreg, Memwrite, multiplexer_1_out, multiplexer_2_out,
       multiplexer_3_out, multiplexer_4_out, multiplexer_5_out, multiplexer_6_out, multiplexer_7_out,
       multiplexer_8_out, multiplexer_9_out, multiplexer_14_out, multiplexer_15_out, multiplexer_16_out,
       multiplexer_17_out, multiplexer_20_out, multiplexer_21_out, not_1_out, Regwrite, Zero;
  wire [4:0] multiplexer_18_out, multiplexer_19_out, Regdst;
  wire [15:0] counter_1_q, main_1_output, multiplexer_13_out, multiplexer_22_out, multiplexer_23_out,
       multiplexer_24_out, multiplexer_30_out, Next_Pc, ram_1_data, register_1_readdata1,
       register_1_readdata2;

  Multiplexer #(.select(4), .enable("false")) multiplexer_1 (
    .in0(1'b0), .in1(1'b1), .in2(Zero), .in3(Zero), .in4(1'b0), .in5(1'b0), .in6(1'b0), .in7(1'b0),
    .in8(1'b0), .in9(1'b0), .in10(1'b0), .in11(1'b0), .in12(1'b0), .in13(1'b0), .in14(1'b0), .in15(1'b0),
    .out(multiplexer_1_out), .sel(Instruction[30:27]));
  not not_1 (not_1_out, multiplexer_2_out);
  Clock clock_1 (.out(Clock));
  Multiplexer #(.enable("false")) multiplexer_2 (
    .in0(multiplexer_1_out), .in1(multiplexer_5_out), .out(multiplexer_2_out), .sel(Instruction[31]));
  Counter #(.width(16), .max('hffff)) counter_1 (
    .load(multiplexer_2_out), .D(Next_Pc), .count(not_1_out), .Q(counter_1_q), .clk(Clock), .clr(in_1));  // open: carry
  Multiplexer #(.select(4), .enable("false")) multiplexer_3 (
    .in0(1'b0), .in1(1'b0), .in2(1'b1), .in3(1'b0), .in4(1'b0), .in5(1'b0), .in6(1'b0), .in7(1'b0),
    .in8(1'b0), .in9(1'b0), .in10(1'b0), .in11(1'b0), .in12(1'b0), .in13(1'b0), .in14(1'b0), .in15(1'b0),
    .out(multiplexer_3_out), .sel(Instruction[30:27]));
  Multiplexer #(.select(4), .enable("false")) multiplexer_4 (
    .in0(1'b0), .in1(1'b0), .in2(1'b0), .in3(1'b0), .in4(1'b0), .in5(1'b0), .in6(1'b0), .in7(1'b0),
    .in8(1'b0), .in9(1'b0), .in10(1'b0), .in11(1'b0), .in12(1'b0), .in13(1'b0), .in14(1'b0), .in15(1'b0),
    .out(multiplexer_4_out), .sel(Instruction[29:26]));
  Multiplexer #(.select(4), .enable("false")) multiplexer_5 (
    .in0(1'b0), .in1(1'b0), .in2(1'b0), .in3(1'b0), .in4(1'b0), .in5(1'b0), .in6(1'b0), .in7(1'b0),
    .in8(1'b0), .in9(1'b0), .in10(1'b0), .in11(1'b0), .in12(1'b0), .in13(1'b0), .in14(1'b0), .in15(1'b0),
    .out(multiplexer_5_out), .sel(Instruction[30:27]));
  Multiplexer #(.select(4), .enable("false")) multiplexer_6 (
    .in0(1'b0), .in1(1'b0), .in2(1'b0), .in3(1'b1), .in4(1'b1), .in5(1'b0), .in6(1'b0), .in7(1'b0),
    .in8(1'b0), .in9(1'b0), .in10(1'b0), .in11(1'b0), .in12(1'b0), .in13(1'b0), .in14(1'b0), .in15(1'b0),
    .out(multiplexer_6_out), .sel(Instruction[30:27]));
  Multiplexer #(.select(4), .enable("false")) multiplexer_7 (
    .in0(1'b0), .in1(1'b0), .in2(1'b0), .in3(1'b1), .in4(1'b0), .in5(1'b0), .in6(1'b0), .in7(1'b1),
    .in8(1'b0), .in9(1'b0), .in10(1'b0), .in11(1'b0), .in12(1'b0), .in13(1'b0), .in14(1'b0), .in15(1'b0),
    .out(multiplexer_7_out), .sel(Instruction[29:26]));
  Multiplexer #(.select(4), .enable("false")) multiplexer_8 (
    .in0(1'b1), .in1(1'b0), .in2(1'b0), .in3(1'b0), .in4(1'b1), .in5(1'b1), .in6(1'b1), .in7(1'b1),
    .in8(1'b1), .in9(1'b1), .in10(1'b1), .in11(1'b1), .in12(1'b1), .in13(1'b1), .in14(1'b1), .in15(1'b1),
    .out(multiplexer_8_out), .sel(Instruction[30:27]));
  Multiplexer #(.select(4), .enable("false")) multiplexer_9 (
    .in0(1'b1), .in1(1'b1), .in2(1'b1), .in3(1'b1), .in4(1'b1), .in5(1'b1), .in6(1'b0), .in7(1'b0),
    .in8(1'b0), .in9(1'b0), .in10(1'b1), .in11(1'b0), .in12(1'b0), .in13(1'b0), .in14(1'b0), .in15(1'b1),
    .out(multiplexer_9_out), .sel(Instruction[29:26]));
  ROM #(.addrWidth(16), .dataWidth(32)) rom_1 (.addr(counter_1_q), .data(Instruction));  // open: sel
  Multiplexer #(.enable("false")) multiplexer_10 (
    .in0(multiplexer_3_out), .in1(multiplexer_4_out), .out(Branch), .sel(Instruction[31]));
  Multiplexer #(.enable("false")) multiplexer_11 (
    .in0(multiplexer_6_out), .in1(multiplexer_7_out), .out(AluSrc), .sel(Instruction[31]));
  Multiplexer #(.enable("false")) multiplexer_12 (
    .in0(multiplexer_8_out), .in1(multiplexer_9_out), .out(Regwrite), .sel(Instruction[31]));
  Register register_1 (
    .ReadAddress1(Instruction[23:21]), .ReadAddress2(Instruction[18:16]), .WriteEnable(Regwrite),
    .ReadData1(register_1_readdata1), .WriteAddress(Regdst[2:0]), .ReadData2(register_1_readdata2),
    .RegisterData(multiplexer_30_out), .Clockin(Clock));
  Multiplexer #(.width(16), .enable("false")) multiplexer_13 (
    .in0(register_1_readdata2), .in1(Instruction[15:0]), .out(multiplexer_13_out), .sel(AluSrc));
  Multiplexer #(.select(4), .enable("false")) multiplexer_14 (
    .in0(1'b0), .in1(1'b0), .in2(1'b0), .in3(1'b0), .in4(1'b0), .in5(1'b0), .in6(1'b0), .in7(1'b0),
    .in8(1'b0), .in9(1'b0), .in10(1'b0), .in11(1'b0), .in12(1'b0), .in13(1'b0), .in14(1'b0), .in15(1'b0),
    .out(multiplexer_14_out), .sel(Instruction[30:27]));
  Multiplexer #(.select(4), .enable("false")) multiplexer_15 (
    .in0(1'b0), .in1(1'b0), .in2(1'b0), .in3(1'b1), .in4(1'b0), .in5(1'b0), .in6(1'b0), .in7(1'b0),
    .in8(1'b0), .in9(1'b0), .in10(1'b0), .in11(1'b0), .in12(1'b0), .in13(1'b0), .in14(1'b0), .in15(1'b0),
    .out(multiplexer_15_out), .sel(Instruction[29:26]));
  Multiplexer #(.select(4), .enable("false")) multiplexer_16 (
    .in0(1'b0), .in1(1'b0), .in2(1'b0), .in3(1'b0), .in4(1'b0), .in5(1'b0), .in6(1'b0), .in7(1'b0),
    .in8(1'b0), .in9(1'b0), .in10(1'b0), .in11(1'b0), .in12(1'b0), .in13(1'b0), .in14(1'b0), .in15(1'b0),
    .out(multiplexer_16_out), .sel(Instruction[30:27]));
  Multiplexer #(.select(4), .enable("false")) multiplexer_17 (
    .in0(1'b0), .in1(1'b0), .in2(1'b0), .in3(1'b0), .in4(1'b0), .in5(1'b0), .in6(1'b0), .in7(1'b0),
    .in8(1'b0), .in9(1'b0), .in10(1'b0), .in11(1'b1), .in12(1'b0), .in13(1'b0), .in14(1'b0), .in15(1'b0),
    .out(multiplexer_17_out), .sel(Instruction[29:26]));
  Multiplexer #(.select(4), .width(5), .enable("false")) multiplexer_18 (
    .in0(Instruction[15:11]), .in4(Instruction[20:16]), .in12(Instruction[15:11]), .out(multiplexer_18_out),
    .sel(Instruction[30:27]));  // open: in1, in2, in3, in5, in6, in7, in8, in9, in10, in11, in13, in14, in15
  Multiplexer #(.select(4), .width(5), .enable("false")) multiplexer_19 (
    .in0(Instruction[15:11]), .in2(Instruction[15:11]), .in3(Instruction[20:16]), .in4(Instruction[15:11]),
    .in5(Instruction[15:11]), .in10(Instruction[15:11]), .in11(Instruction[20:16]),
    .in15(Instruction[15:11]), .out(multiplexer_19_out), .sel(Instruction[29:26]));  // open: in1, in6, in7, in8, in9, in12, in13, in14
  Multiplexer #(.select(4), .enable("false")) multiplexer_20 (
    .in0(1'b0), .in1(1'b0), .in2(1'b0), .in3(1'b0), .in4(1'b0), .in5(1'b0), .in6(1'b0), .in7(1'b0),
    .in8(1'b0), .in9(1'b0), .in10(1'b0), .in11(1'b0), .in12(1'b0), .in13(1'b0), .in14(1'b0), .in15(1'b0),
    .out(multiplexer_20_out), .sel(Instruction[30:27]));
  Multiplexer #(.select(4), .enable("false")) multiplexer_21 (
    .in0(1'b0), .in1(1'b0), .in2(1'b0), .in3(1'b1), .in4(1'b0), .in5(1'b0), .in6(1'b0), .in7(1'b0),
    .in8(1'b0), .in9(1'b0), .in10(1'b0), .in11(1'b0), .in12(1'b0), .in13(1'b0), .in14(1'b0), .in15(1'b0),
    .out(multiplexer_21_out), .sel(Instruction[29:26]));
  Multiplexer #(.width(16), .enable("false")) multiplexer_22 (
    .in0(counter_1_q), .in1(Instruction[15:0]), .out(multiplexer_22_out), .sel(Zero));
  Multiplexer #(.select(4), .width(16), .enable("false")) multiplexer_23 (
    .in0(counter_1_q), .in1(Instruction[15:0]), .in2(multiplexer_22_out), .in3(multiplexer_22_out),
    .in4(counter_1_q), .in5(counter_1_q), .in6(counter_1_q), .in7(counter_1_q), .in8(counter_1_q),
    .in9(counter_1_q), .in10(counter_1_q), .in11(counter_1_q), .in12(counter_1_q), .in13(counter_1_q),
    .in14(counter_1_q), .in15(counter_1_q), .out(multiplexer_23_out), .sel(Instruction[30:27]));
  Multiplexer #(.select(4), .width(16), .enable("false")) multiplexer_24 (
    .in0(counter_1_q), .in1(counter_1_q), .in2(counter_1_q), .in3(counter_1_q), .in4(counter_1_q),
    .in5(counter_1_q), .in6(counter_1_q), .in7(counter_1_q), .in8(counter_1_q), .in9(counter_1_q),
    .in10(counter_1_q), .in11(counter_1_q), .in12(counter_1_q), .in13(counter_1_q), .in14(counter_1_q),
    .in15(counter_1_q), .out(multiplexer_24_out), .sel(Instruction[29:26]));
  main main_1 (
    .Input_A(register_1_readdata1), .Input_B(multiplexer_13_out), .Output(main_1_output),
    .Opcode(Instruction[31:26]), .Zero(Zero));  // open: Overflow, Carryout
  Multiplexer #(.enable("false")) multiplexer_25 (
    .in0(multiplexer_14_out), .in1(multiplexer_15_out), .out(Memrd), .sel(Instruction[31]));
  Multiplexer #(.enable("false")) multiplexer_26 (
    .in0(multiplexer_16_out), .in1(multiplexer_17_out), .out(Memwrite), .sel(Instruction[31]));
  Multiplexer #(.width(5), .enable("false")) multiplexer_27 (
    .in0(multiplexer_18_out), .in1(multiplexer_19_out), .out(Regdst), .sel(Instruction[31]));
  Multiplexer #(.enable("false")) multiplexer_28 (
    .in0(multiplexer_20_out), .in1(multiplexer_21_out), .out(Memtoreg), .sel(Instruction[31]));
  RAM #(.dataWidth(16), .bus("separate")) ram_1 (
    .addr(main_1_output[7:0]), .din(register_1_readdata2), .data(ram_1_data), .str(Memwrite), .clk(Clock),
    .ld(Memrd));  // open: sel, clr
  Multiplexer #(.width(16), .enable("false")) multiplexer_29 (
    .in0(multiplexer_23_out), .in1(multiplexer_24_out), .out(Next_Pc), .sel(Instruction[31]));
  Multiplexer #(.width(16), .enable("false")) multiplexer_30 (
    .in0(main_1_output), .in1(ram_1_data), .out(multiplexer_30_out), .sel(Memtoreg));

  // Other names for the same wires on the sheet: func[5:0] = Instruction[5:0]; immediate[15:0] = Instruction[15:0];
  //   JumpTarget[25:0] = Instruction[25:0]; shamt[4:0] = Instruction[10:6]; rd[4:0] = Instruction[15:11];
  //   rt[4:0] = Instruction[20:16]; rs[4:0] = Instruction[25:21]; Opcode[5:0] = Instruction[31:26]; Reset = in_1

  // Notes on the sheet:
  //   contents of rom_1 (hex, n*v repeats v):
  //   0 2042fffb fc400800
endmodule

// myinst
module abstract_value (
  input  [15:0] Input,
  output [15:0] Output,
  output [15:0] Flipped
);

  wire [15:0] n16bitadder_1__16_bit_output;

  _16BitAdder u_16bitadder_1 (
    ._16_bit_A(16'h1), ._16_bit_B(Flipped), ._16_bit_output(n16bitadder_1__16_bit_output));  // open: Carryout, Overflow
  not not_1 (Flipped[0], Input[0]);
  not not_2 (Flipped[1], Input[1]);
  not not_3 (Flipped[2], Input[2]);
  not not_4 (Flipped[3], Input[3]);
  not not_5 (Flipped[4], Input[4]);
  not not_6 (Flipped[5], Input[5]);
  not not_7 (Flipped[6], Input[6]);
  Multiplexer #(.width(16), .enable("false")) multiplexer_1 (
    .in0(Input), .in1(n16bitadder_1__16_bit_output), .out(Output), .sel(Input[15]));
  not not_8 (Flipped[7], Input[7]);
  not not_9 (Flipped[8], Input[8]);
  not not_10 (Flipped[9], Input[9]);
  not not_11 (Flipped[10], Input[10]);
  not not_12 (Flipped[11], Input[11]);
  not not_13 (Flipped[12], Input[12]);
  not not_14 (Flipped[13], Input[13]);
  not not_15 (Flipped[14], Input[14]);
  not not_16 (Flipped[15], Input[15]);

  // Other names for the same wires on the sheet: Flip[15:0] = Flipped
endmodule
